// Logisim project computer.circ as structural Verilog: 1 circuit, main circuit main
module main (
);

  wire and_1_out, and_2_out, and_3_out, and_4_out, and_5_out, and_8_out, and_9_out, Block_Storage_1_p5,
       BSRead, BusReq, clock_1_out, clock_2_out, clock_3_out, clock_5_out, comparator_1_eq, comparator_2_eq,
       comparator_3_eq, comparator_4_eq, comparator_5_eq, comparator_6_eq, comparator_7_eq, DMAMemRead,
       DMAMemWrite, ExternalIntReq, Keyboard_1_avail, MemRead, MemWrite, RAMRead, rv32im_cpu_1_p8,
       rv32im_cpu_1_p9, rv32im_cpu_1_p10, timer_1_p4, TimerIntReq;
  wire [3:0] DMABE, multiplexer_5_out, undriven;
  wire [6:0] Keyboard_1_data;
  wire [31:0] Address, bit_extender_1_out, bit_extender_2_out, DMAAddress, DMAWData, multiplexer_6_out,
       multiplexer_7_out, multiplexer_8_out, multiplexer_9_out, multiplexer_10_out, RAM_1_dout, RData,
       ROM_1_data, rv32im_cpu_1_p6, rv32im_cpu_1_p7, timer_1_p6, WData;

  Clock clock_1 (.out(clock_1_out));
  Clock clock_2 (.out(clock_2_out));
  Comparator #(.width(32)) comparator_1 (.a(Address), .b(32'hffff000c), .eq(comparator_1_eq));  // open: gt, lt
  and and_1 (and_1_out, comparator_1_eq, MemWrite);
  // RV32IM_CPU #(.hexRegisters("true"), .tlbEntries(16)) rv32im_cpu_1: pin names not known; wires that end beside it: clock_1_out, RData, TimerIntReq, ExternalIntReq, BusReq, rv32im_cpu_1_p6, rv32im_cpu_1_p7, rv32im_cpu_1_p8, rv32im_cpu_1_p9, rv32im_cpu_1_p10
  TTY #(.cols(80), .rows(12)) TTY_1 (.data(WData[6:0]), .clk(clock_2_out), .we(and_1_out));  // open: clr
  Comparator #(.width(32)) comparator_2 (.a(Address), .b(32'hffff0008), .eq(comparator_2_eq));  // open: gt, lt
  Clock clock_3 (.out(clock_3_out));
  Keyboard Keyboard_1 (
    .clk(clock_3_out), .re(and_2_out), .avail(Keyboard_1_avail), .data(Keyboard_1_data));  // open: clr
  and and_2 (and_2_out, comparator_2_eq, MemRead);
  Comparator #(.width(32)) comparator_3 (.a(Address), .b(32'hffff0004), .eq(comparator_3_eq));  // open: gt, lt
  assign bit_extender_1_out = {{25{1'b0}}, Keyboard_1_data};  // Bit_Extender bit_extender_1
  assign bit_extender_2_out = {{31{1'b0}}, Keyboard_1_avail};  // Bit_Extender bit_extender_2
  and and_3 (and_3_out, comparator_3_eq, MemRead);
  Multiplexer #(.width(32)) multiplexer_1 (
    .in0(rv32im_cpu_1_p6), .in1(DMAAddress), .out(Address), .sel(rv32im_cpu_1_p10));
  Multiplexer #(.width(32)) multiplexer_2 (.in0(rv32im_cpu_1_p7), .in1(DMAWData), .out(WData), .sel(rv32im_cpu_1_p10));
  Multiplexer multiplexer_3 (.in0(rv32im_cpu_1_p8), .in1(DMAMemRead), .out(MemRead), .sel(rv32im_cpu_1_p10));
  Multiplexer multiplexer_4 (.in0(rv32im_cpu_1_p9), .in1(DMAMemWrite), .out(MemWrite), .sel(rv32im_cpu_1_p10));
  Multiplexer #(.width(4)) multiplexer_5 (.in0(undriven), .in1(DMABE), .out(multiplexer_5_out), .sel(rv32im_cpu_1_p10));
  Multiplexer #(.width(32)) multiplexer_6 (
    .in0({32{1'b0}}), .in1(bit_extender_1_out), .out(multiplexer_6_out), .sel(and_2_out));
  Multiplexer #(.width(32)) multiplexer_7 (
    .in0(multiplexer_6_out), .in1(bit_extender_2_out), .out(multiplexer_7_out), .sel(and_3_out));
  Comparator #(.mode("unsigned"), .width(12)) comparator_4 (
    .a(Address[31:20]), .b(12'h1), .eq(comparator_4_eq));  // open: gt, lt
  Comparator #(.mode("unsigned"), .width(16)) comparator_5 (
    .a(Address[31:16]), .b(16'h200), .eq(comparator_5_eq));  // open: gt, lt
  // Timer timer_1: pin names not known; wires that end beside it: Address, MemRead, MemWrite, timer_1_p4, WData, timer_1_p6, TimerIntReq
  Clock clock_4 (.out(timer_1_p4));
  Comparator #(.mode("unsigned"), .width(16)) comparator_6 (
    .a(Address[31:16]), .b({16{1'b0}}), .eq(comparator_6_eq));  // open: gt, lt
  and and_4 (and_4_out, comparator_6_eq, MemRead);
  and and_5 (and_5_out, MemWrite, comparator_4_eq);
  and and_6 (RAMRead, comparator_4_eq, MemRead);
  and and_7 (BSRead, MemRead, comparator_7_eq);
  Comparator #(.mode("unsigned"), .width(24)) comparator_7 (
    .a(Address[31:8]), .b(24'h2000), .eq(comparator_7_eq));  // open: gt, lt
  and and_8 (and_8_out, comparator_7_eq, MemWrite);
  and and_9 (and_9_out, MemRead, comparator_5_eq);
  Multiplexer #(.width(32)) multiplexer_8 (
    .in0(multiplexer_7_out), .in1(timer_1_p6), .out(multiplexer_8_out), .sel(and_9_out));
  ROM #(.addrWidth(14), .dataWidth(32)) ROM_1 (.addr(Address[15:2]), .data(ROM_1_data));
  RAM #(.addrWidth(18), .asyncread("true"), .byteenables("byteEnables"), .dataWidth(32), .fpgaMemory("sdram")) RAM_1 (
    .addr(Address[19:2]), .we(and_5_out), .oe(RAMRead), .clk(clock_5_out), .din(WData), .dout(RAM_1_dout),
    .be3(multiplexer_5_out[3]), .be2(multiplexer_5_out[2]), .be1(multiplexer_5_out[1]),
    .be0(multiplexer_5_out[0]));
  Clock clock_5 (.out(clock_5_out));
  // Block_Storage Block_Storage_1: pin names not known; wires that end beside it: BSRead, and_8_out, WData, rv32im_cpu_1_p10, Block_Storage_1_p5, DMAWData, RData, DMAMemRead, DMAMemWrite, DMAAddress, BusReq
  Clock clock_6 (.out(Block_Storage_1_p5));
  Multiplexer #(.width(32)) multiplexer_9 (
    .in0(multiplexer_8_out), .in1(ROM_1_data), .out(multiplexer_9_out), .sel(and_4_out));
  Multiplexer #(.width(32)) multiplexer_10 (
    .in0(multiplexer_9_out), .in1(RAM_1_dout), .out(multiplexer_10_out), .sel(RAMRead));
  Multiplexer #(.width(32)) multiplexer_11 (.in0(multiplexer_10_out), .in1(DMAWData), .out(RData), .sel(BSRead));

  // Notes on the sheet:
  //   Display:
  //   Keyboard:
  //   BusAck 0: CPU, 1: DMA
  //   Read chain: 0, or the data of the device that is read
  //   contents of ROM_1 (hex, n*v repeats v):
  //   200117 ffc10113 1f0297 ff828293 1f0317 3f030313 62d863 2a023 428293 ff5ff06f 513 593 613 8000ef 6f
  //   f4010113 a112e23 a812c23 b512223 1517 8bc50513 2fc000ef 1f0597 fa858593 513 2a4000ef 10051663 1f0717
  //   f9472703 534657b7 34678793 10f71663 1517 8e450513 2c8000ef 8c10693 1f0617 17060613 1f0597 f6858593
  //   1517 8dc50513 450000ef e051863 1517 8fc50513 298000ef 8c12503 314000ef 1517 8e450513 284000ef
  //   8c12503 357413 741413 255513 1f0597 12058593 1f0797 f347a783 f50533 214000ef c051863 8000613 1f0597
  //   10058593 8585b3 c10513 794000ef c12a83 1517 8d850513 230000ef a8513 2ac000ef 1517 8d850513 21c000ef
  //   a0a8263 a912a23 b212823 b312623 b412423 b612023 9712e23 1410913 a13 1009b7 413 20000b13 1b97
  //   8c0b8b93 ac0006f 517 7ac50513 1d4000ef 2e0000ef ee9ff06f 517 7bc50513 1c0000ef 2cc000ef ee9ff06f 517
  //   7f050513 1ac000ef 517 7d450513 1a0000ef 517 7f450513 194000ef 2a0000ef eedff06f 1517 80450513
  //   180000ef 28c000ef f25ff06f 1517 83050513 16c000ef 278000ef a8413 880006f 98593 110000ef 2051c63
  //   20098993 940433 1a0a13 290913 3ca2793 c078c63 3547663 95503 4050063 408a84b3 fc9b76e3 b0493 fc5ff06f
  //   b8513 118000ef 224000ef fc1ff06f b412483 b012903 ac12983 a812a03 a012b03 9c12b83 1c0006f b412483
  //   b012903 ac12983 a812a03 a012b03 9c12b83 517 7d450513 d0000ef 40513 14c000ef 517 7d050513 bc000ef
  //   100537 d8000ef 517 70850513 a8000ef 517 7c050513 9c000ef 100537 b8000ef 517 7cc50513 88000ef 1007b7
  //   780e7 18c000ef bc12083 b812403 a412a83 c010113 8067 b412483 b012903 ac12983 a812a03 a012b03 9c12b83
  //   f75ff06f 2007b7 b7a223 a7a423 100713 e7a023 c78713 100693 72783 fed78ee3 2007b7 c7a503 ffd50513
  //   153513 40a00533 8067 ffff07b7 a7a623 8067 54783 78e63 ffff0737 c70713 150513 f72023 54783 fe079ae3
  //   8067 693 1c00713 900813 ffff0637 c60613 ffc00593 100893 200006f 5778693 f84463 3078693 d62023
  //   ffc70713 2b70463 88693 e557b3 f7f793 d7e6b3 fc069ce3 fc070ae3 ffc70713 693 fe5ff06f 8067 6050e63
  //   ff010113 713 410893 ccccd5b7 ccd58593 900813 170713 e88633 2b536b3 36d693 269793 d787b3 179793
  //   40f507b3 3078793 fef60fa3 50793 68513 fcf868e3 2e05263 410613 e607b3 ffff06b7 c68693 fff7c703 e6a023
  //   fff78793 fef61ae3 1010113 8067 ffff07b7 3000713 e7a623 8067 ff010113 112623 517 62850513 ee1ff0ef 6f
  //   fe010113 112e23 812c23 912a23 1212823 1312623 50413 60913 68993 255513 1c5a783 60593 f50533 e5dff0ef
  //   4051063 50493 347413 741593 8000613 b905b3 98513 3d8000ef 48513 1c12083 1812403 1412483 1012903
  //   c12983 2010113 8067 fff00493 fddff06f f1010113 e112623 b12423 d12623 20050e63 d912223 60c93 54703
  //   2f00793 20f71863 d312e23 154783 150993 813 4078063 e812423 e912223 f212023 d412c23 d512a23 d612823
  //   d712623 d812423 da12023 bb12e23 1410b93 70c13 3010d13 200d93 580006f c12783 7a023 513 dc12983
  //   c412c83 1500006f 190913 148493 2040413 1092793 c078863 d44f663 42783 fe0782e3 b8593 440513 32c000ef
  //   fc051ae3 42803 9c783 12078463 9c703 10070c63 fd170693 793 10068663 198993 178793 fb86b3 fee68fa3
  //   9c703 e036b3 fd170613 c03633 c6f6b3 68663 1b7a693 fc069ae3 a078793 1010713 e787b3 f6078223 9c783
  //   1879863 198993 9c783 ff878ce3 d0693 c8613 812583 80513 e3dff0ef 50a93 4051e63 3414783 5b79a63
  //   3012a03 5a5a13 40a0463 3810b13 493 180006f 1a8a93 2b0b13 3caa793 2078663 344f463 b5503 fe0504e3
  //   c8593 c81ff0ef 50913 51863 144f663 c8413 f05ff06f fff00513 e812403 e412483 e012903 dc12983 d812a03
  //   d412a83 d012b03 cc12b83 c812c03 c412c83 c012d03 bc12d83 ec12083 f010113 8067 793 f25ff06f c12783
  //   107a023 e812403 e412483 e012903 dc12983 d812a03 d412a83 d012b03 cc12b83 c812c03 c412c83 c012d03
  //   bc12d83 fb5ff06f fff00513 fadff06f fff00513 c412c83 fa1ff06f f5010113 a112623 a912223 b212023
  //   9312e23 9512a23 60a93 68913 70993 78493 10693 d15ff0ef 10051c63 12783 ef97063 9412c23 990733 2e7f663
  //   a812423 9612823 9712623 9812423 412784b3 a13 3b00b13 810b93 20000c13 400006f 8048463 a812423 9612823
  //   9712623 9812423 fd9ff06f 40613 ba85b3 98513 d8000ef 8989b3 890933 408484b3 8a0a33 2048e63 995813
  //   50b6863 181813 1780833 85503 6050a63 a8593 b09ff0ef 8051263 1ff97593 40bc0433 fa84f8e3 48413
  //   fa9ff06f a812403 9012b03 8c12b83 8812c03 1c0006f 48a13 140006f a812403 9012b03 8c12b83 8812c03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
endmodule
