// Logisim project multitasking.circ as structural Verilog: 1 circuit, main circuit main
module main (
);

  wire and_2_out, and_3_out, and_4_out, and_5_out, and_6_out, and_7_out, and_8_out, and_9_out, and_10_out,
       and_11_out, and_12_out, and_13_out, button_1_out, clock_1_out, clock_3_out, clock_4_out, clock_5_out,
       clock_7_out, clock_8_out, clock_9_out, comparator_1_eq, comparator_2_eq, comparator_3_eq,
       comparator_4_eq, comparator_5_eq, comparator_6_eq, comparator_7_eq, comparator_8_eq, comparator_9_eq,
       keyboard_1_avail, MemRead, MemWrite, or_1_out, por_1_out, rgb_video_1_p2, rgb_video_1_p3, timer_1_p6,
       TimerIRQ;
  wire [6:0] keyboard_1_data;
  wire [31:0] Address, bit_extender_1_out, bit_extender_2_out, DataIn, DataOut, ram_1_dout, ram_2_dout,
       ram_3_dout, ram_4_dout, rom_1_data;

  POR por_1 (.out(por_1_out));
  or or_1 (or_1_out, por_1_out, button_1_out);
  Button button_1 (.out(button_1_out));
  Clock clock_1 (.out(clock_1_out));
  // RGB_Video #(.cursor("No Cursor"), .height(32), .scale(8), .width(32)) rgb_video_1: pin names not known; wires that end beside it: or_1_out, rgb_video_1_p2, rgb_video_1_p3, Address[6:2], Address[11:7]
  Clock clock_2 (.out(rgb_video_1_p2));
  and and_1 (rgb_video_1_p3, comparator_1_eq, MemWrite);
  Comparator #(.width(20)) comparator_1 (.a(20'hffff8), .b(Address[31:12]), .eq(comparator_1_eq));  // open: gt, lt
  // RV32IM_CPU #(.hexRegisters("true"), .tcpPort(3334)) rv32im_cpu_1: pin names not known; wires that end beside it: clock_1_out, or_1_out, DataIn, TimerIRQ, Address, DataOut, MemRead, MemWrite
  Clock clock_3 (.out(clock_3_out));
  ROM #(.addrWidth(14), .dataWidth(32)) rom_1 (.addr(Address[15:2]), .data(rom_1_data));
  Comparator #(.width(16)) comparator_2 (.a(Address[31:16]), .b({16{1'b0}}), .eq(comparator_2_eq));  // open: gt, lt
  RAM #(.addrWidth(14), .asyncread("true"), .dataWidth(32)) ram_1 (
    .addr(Address[15:2]), .we(and_4_out), .clk(clock_3_out), .din(DataOut), .dout(ram_1_dout));  // open: oe
  Comparator #(.width(16)) comparator_3 (.a(Address[31:16]), .b(16'h1), .eq(comparator_3_eq));  // open: gt, lt
  Comparator #(.width(32)) comparator_4 (.a(Address), .b(32'hffff0000), .eq(comparator_4_eq));  // open: gt, lt
  Comparator #(.mode("unsigned"), .width(32)) comparator_5 (
    .a(Address), .b(32'hffff0008), .eq(comparator_5_eq));  // open: gt, lt
  Comparator #(.mode("unsigned"), .width(32)) comparator_6 (
    .a(Address), .b(32'hffff0004), .eq(comparator_6_eq));  // open: gt, lt
  and and_2 (and_2_out, comparator_2_eq, MemRead);
  and and_3 (and_3_out, comparator_3_eq, MemRead);
  and and_4 (and_4_out, comparator_3_eq, MemWrite);
  TTY tty_1 (.data(DataOut[6:0]), .clk(clock_4_out), .we(and_5_out));  // open: clr
  Clock clock_4 (.out(clock_4_out));
  and and_5 (and_5_out, comparator_4_eq, MemWrite);
  Clock clock_5 (.out(clock_5_out));
  Keyboard keyboard_1 (
    .clk(clock_5_out), .re(and_6_out), .avail(keyboard_1_avail), .data(keyboard_1_data));  // open: clr
  and and_6 (and_6_out, comparator_5_eq, MemRead);
  and and_7 (and_7_out, comparator_6_eq, MemRead);
  // Timer timer_1: pin names not known; wires that end beside it: Address, MemWrite, MemRead, DataOut, or_1_out, timer_1_p6, DataIn, TimerIRQ, DataIn
  Clock clock_6 (.out(timer_1_p6));
  assign DataIn = and_2_out ? rom_1_data : 32'bz;  // Controlled_Buffer controlled_buffer_1
  assign DataIn = and_3_out ? ram_1_dout : 32'bz;  // Controlled_Buffer controlled_buffer_2
  assign bit_extender_1_out = {{25{1'b0}}, keyboard_1_data};  // Bit_Extender bit_extender_1
  assign DataIn = and_6_out ? bit_extender_1_out : 32'bz;  // Controlled_Buffer controlled_buffer_3
  assign bit_extender_2_out = {{31{1'b0}}, keyboard_1_avail};  // Bit_Extender bit_extender_2
  assign DataIn = and_7_out ? bit_extender_2_out : 32'bz;  // Controlled_Buffer controlled_buffer_4
  Clock clock_7 (.out(clock_7_out));
  Clock clock_8 (.out(clock_8_out));
  Clock clock_9 (.out(clock_9_out));
  RAM #(.addrWidth(14), .asyncread("true"), .dataWidth(32)) ram_2 (
    .addr(Address[15:2]), .we(and_9_out), .clk(clock_7_out), .din(DataOut), .dout(ram_2_dout));  // open: oe
  Comparator #(.width(16)) comparator_7 (.a(Address[31:16]), .b(16'h2), .eq(comparator_7_eq));  // open: gt, lt
  and and_8 (and_8_out, comparator_7_eq, MemRead);
  and and_9 (and_9_out, comparator_7_eq, MemWrite);
  RAM #(.addrWidth(14), .asyncread("true"), .dataWidth(32)) ram_3 (
    .addr(Address[15:2]), .we(and_11_out), .clk(clock_8_out), .din(DataOut), .dout(ram_3_dout));  // open: oe
  Comparator #(.width(16)) comparator_8 (.a(Address[31:16]), .b(16'h3), .eq(comparator_8_eq));  // open: gt, lt
  and and_10 (and_10_out, comparator_8_eq, MemRead);
  and and_11 (and_11_out, comparator_8_eq, MemWrite);
  RAM #(.addrWidth(14), .asyncread("true"), .dataWidth(32)) ram_4 (
    .addr(Address[15:2]), .we(and_13_out), .clk(clock_9_out), .din(DataOut), .dout(ram_4_dout));  // open: oe
  Comparator #(.width(16)) comparator_9 (.a(Address[31:16]), .b(16'h4), .eq(comparator_9_eq));  // open: gt, lt
  and and_12 (and_12_out, comparator_9_eq, MemRead);
  and and_13 (and_13_out, comparator_9_eq, MemWrite);
  assign DataIn = and_8_out ? ram_2_dout : 32'bz;  // Controlled_Buffer controlled_buffer_5
  assign DataIn = and_10_out ? ram_3_dout : 32'bz;  // Controlled_Buffer controlled_buffer_6
  assign DataIn = and_12_out ? ram_4_dout : 32'bz;  // Controlled_Buffer controlled_buffer_7

  // Notes on the sheet:
  //   RESET
  //   DataIn
  //   VGA Display
  //   Address
  //   DataOut
  //   MemRead
  //   MemWrite
  //   Supervisor ROM
  //   Supervisor RAM
  //   TTY Display
  //   Keyboard
  //   User 1 RAM
  //   User 2 RAM
  //   User 3 RAM
endmodule
